// Logisim project FIFO.circ as structural Verilog: 4 circuits, main circuit main
module main (
  input  WRITE_EN,
  input  READ_MODE,
  input  RESET,
  input  [9:0] PACKET_IN,
  input  in_5,
  input  READ_EN,
  output [9:0] DATA_OUT,
  output FULL,
  output [3:0] COUNT,
  output EMPTY
);

  wire clock_1_out, undriven;
  wire [2:0] multiplexer_1_out, READ_PTR_read_addr, WRITE_PTR_write_addr;

  Read_Pointer READ_PTR (.READ_EN(READ_EN), .RESET(RESET), .CLK(clock_1_out), .READ_ADDR(READ_PTR_read_addr));
  FIFO_Counter COUNTER (
    .RESET(RESET), .WRITE_EN(WRITE_EN), .READ_EN(READ_EN), .CLK(clock_1_out), .FULL(FULL), .COUNT(COUNT),
    .EMPTY(EMPTY));
  Write_Pointer WRITE_PTR (.WRITE_EN(WRITE_EN), .RESET(RESET), .CLK(clock_1_out), .WRITE_ADDR(WRITE_PTR_write_addr));
  Multiplexer #(.width(3)) multiplexer_1 (
    .in0(WRITE_PTR_write_addr), .in1(READ_PTR_read_addr), .out(multiplexer_1_out), .sel(READ_MODE));  // open: en
  Clock clock_1 (.out(clock_1_out));
  RAM #(.addrWidth(3), .dataWidth(10), .bus("separate")) ram_1 (
    .addr(multiplexer_1_out), .din(PACKET_IN), .data(DATA_OUT), .sel(in_5), .clk(clock_1_out), .ld(WRITE_EN),
    .clr(undriven));  // open: str
endmodule

module Write_Pointer (
  input  WRITE_EN,
  input  RESET,
  input  CLK,
  output [2:0] WRITE_ADDR
);

  wire [2:0] adder_1_out, multiplexer_1_out, multiplexer_2_out;

  Multiplexer #(.width(3)) multiplexer_1 (
    .in0(WRITE_ADDR), .in1(adder_1_out), .out(multiplexer_1_out), .sel(WRITE_EN));  // open: en
  Multiplexer #(.width(3)) multiplexer_2 (
    .in0(multiplexer_1_out), .in1(3'b000), .out(multiplexer_2_out), .sel(RESET));  // open: en
  Register #(.width(3)) register_1 (.D(multiplexer_2_out), .Q(WRITE_ADDR), .clk(CLK));  // open: en, clr
  Adder #(.width(3)) adder_1 (.a(WRITE_ADDR), .b(3'b001), .out(adder_1_out), .cin(1'b0));  // open: cout
endmodule

module Read_Pointer (
  input  READ_EN,
  input  RESET,
  input  CLK,
  output [2:0] READ_ADDR
);

  wire [2:0] adder_1_out, multiplexer_1_out, multiplexer_2_out;

  Multiplexer #(.width(3)) multiplexer_1 (
    .in0(READ_ADDR), .in1(adder_1_out), .out(multiplexer_1_out), .sel(READ_EN));  // open: en
  Multiplexer #(.width(3)) multiplexer_2 (
    .in0(multiplexer_1_out), .in1(3'b000), .out(multiplexer_2_out), .sel(RESET));  // open: en
  Register #(.width(3)) register_1 (.D(multiplexer_2_out), .Q(READ_ADDR), .clk(CLK));  // open: en, clr
  Adder #(.width(3)) adder_1 (.a(READ_ADDR), .b(3'b001), .out(adder_1_out), .cin(1'b0));  // open: cout
endmodule

module FIFO_Counter (
  input  RESET,
  input  CLK,
  input  WRITE_EN,
  input  READ_EN,
  output FULL,
  output [3:0] COUNT,
  output EMPTY
);

  wire and_1_out, and_2_out, not_1_out, not_2_out, not_3_out, not_4_out, not_5_out, xor_1_out;
  wire [3:0] adder_1_out, adder_2_out, multiplexer_1_out, multiplexer_2_out, multiplexer_3_out;

  and and_1 (and_1_out, not_4_out, WRITE_EN);
  and and_2 (and_2_out, READ_EN, not_5_out);
  Adder #(.width(4)) adder_1 (.a(COUNT), .b(4'b0001), .out(adder_1_out), .cin(1'b0));  // open: cout
  Adder #(.width(4)) adder_2 (.a(4'b1111), .b(COUNT), .out(adder_2_out), .cin(1'b0));  // open: cout
  xor xor_1 (xor_1_out, and_1_out, and_2_out);
  Multiplexer #(.width(4)) multiplexer_1 (
    .in0(adder_2_out), .in1(adder_1_out), .out(multiplexer_1_out), .sel(and_1_out));  // open: en
  Multiplexer #(.width(4)) multiplexer_2 (
    .in0(COUNT), .in1(multiplexer_1_out), .out(multiplexer_2_out), .sel(xor_1_out));  // open: en
  Multiplexer #(.width(4)) multiplexer_3 (
    .in0(multiplexer_2_out), .in1(4'b0000), .out(multiplexer_3_out), .sel(RESET));  // open: en
  Register #(.width(4)) register_1 (.D(multiplexer_3_out), .Q(COUNT), .clk(CLK));  // open: en, clr
  not not_1 (not_1_out, COUNT[0]);
  not not_2 (not_2_out, COUNT[1]);
  not not_3 (not_3_out, COUNT[2]);
  and and_3 (FULL, not_1_out, not_2_out, not_3_out, COUNT[3]);
  nor nor_1 (EMPTY, COUNT[0], COUNT[1], COUNT[2], COUNT[3]);
  not not_4 (not_4_out, FULL);
  not not_5 (not_5_out, EMPTY);
endmodule
